# Fritzing sketch DCPowerSwitch (saved by Fritzing 0.8.3b)
circuit board: 4.96708cm x 2.60584cm
breadboards: 1

parts:
  1K = Resistor [tolerance=±5% resistance=220 package=THT]
  1K_2 = Resistor [tolerance=±5% resistance=220 package=THT]
  1K_3 = Resistor [tolerance=±5% resistance=220 package=THT]
  IN = male pin header, 5 pins [form="♂ (male)"]
  FET1 = pnp-Powertransistor [package="TO220 [THT]"]
  FET2 = pnp-Powertransistor [package="TO220 [THT]"]
  FET3 = pnp-Powertransistor [package="TO220 [THT]"]
  D3 = Rectifier Diode [part_number=1N4001 package="300 mil [THT]"]
  D2 = Rectifier Diode [part_number=1N4001 package="300 mil [THT]"]
  D1 = Rectifier Diode [part_number=1N4001 package="300 mil [THT]"]
  J1 = Screw terminal - 2 pins [package=THT]
  J2 = Screw terminal - 2 pins [package=THT]
  J3 = Screw terminal - 2 pins [package=THT]
  LED1 = LED - 3mm [color="Red (633nm)" package="3 mm [THT]"]
  LED2 = LED - 3mm [color="Red (633nm)" package="3 mm [THT]"]
  LED3 = LED - 3mm [color="Red (633nm)" package="3 mm [THT]"]

nets:
  N1: 1K.Pin_0, IN.pin1
  N2: 1K.Pin_1, LED2.anode
  N3: 1K_2.Pin_0, IN.pin2
  N4: 1K_2.Pin_1, LED1.anode
  N5: 1K_3.Pin_0, IN.pin3
  N6: 1K_3.Pin_1, LED3.anode
  N7: IN.pin4, D3.cathode, D2.cathode, D1.cathode, J1.pin1, J2.pin1, J3.pin1
  N8: FET1.base, LED2.cathode
  N9: FET1.collector, D1.anode, J1.pin2
  N10: FET2.base, LED1.cathode
  N11: FET2.collector, D2.anode, J2.pin2
  N12: FET3.base, LED3.cathode
  N13: FET3.collector, D3.anode, J3.pin2

notes:
  exsertus.com
  DCPowerSwitch v1.0
  +
  P1 P2 P3 Vcc GND
