# Fritzing sketch XBeeDCPowerSwitch84_1.0 (saved by Fritzing 0.8.3b)
circuit board: 5.5786cm x 6.08658cm
breadboards: 1

parts:
  Actv = LED - 3mm [color="Red (633nm)" package="3 mm [THT]"]
  RSSI = LED - 3mm [color="Red (633nm)" package="3 mm [THT]"]
  Assc = LED - 3mm [color="Red (633nm)" package="3 mm [THT]"]
  XBee = XBee
  Attiny84 = IC, DIP package, 14 pins [chip_label=Attiny84]
  220 = Resistor [tolerance=±5% resistance=220 package=THT]
  220_2 = Resistor [tolerance=±5% resistance=220 package=THT]
  220_3 = Resistor [tolerance=±5% resistance=220 package=THT]
  220_4 = Resistor [tolerance=±5% resistance=220 package=THT]
  220_5 = Resistor [tolerance=±5% resistance=220 package=THT]
  220_6 = Resistor [tolerance=±5% resistance=220 package=THT]
  FET4 = pnp-Powertransistor [package="TO220 [THT]"]
  FET5 = pnp-Powertransistor [package="TO220 [THT]"]
  FET6 = pnp-Powertransistor [package="TO220 [THT]"]
  D2 = Rectifier Diode [part_number=1N4001 package="300 mil [THT]"]
  D1 = Rectifier Diode [part_number=1N4001 package="300 mil [THT]"]
  D3 = Rectifier Diode [part_number=1N4001 package="300 mil [THT]"]
  J4 = Screw terminal - 2 pins [package=THT]
  J5 = Screw terminal - 2 pins [package=THT]
  J6 = Screw terminal - 2 pins [package=THT]
  LED4 = LED - 3mm [color="Red (633nm)" package="3 mm [THT]"]
  LED5 = LED - 3mm [color="Red (633nm)" package="3 mm [THT]"]
  LED6 = LED - 3mm [color="Red (633nm)" package="3 mm [THT]"]
  Power_plug1 = Power plug
  U1 = Voltage Regulator - 3.3V [package="TO220 [THT]"]
  J7 = male pin header, 3 pins [form="♂ (male)"]
  Sensor2 = female pin header, 4 pins [form="♀ (female)"]

nets:
  N1: Actv.anode, 220_3.Pin_0
  N2: RSSI.anode, 220_2.Pin_1
  N3: Assc.anode, 220.Pin_1
  N4: XBee.VCC, Attiny84.pin1, U1.output_voltage, J7.pin2, Sensor2.pin1
  N5: XBee.pin2, Attiny84.pin5
  N6: XBee.pin3, Attiny84.pin6
  N7: XBee.pin6, 220_2.Pin_0
  N8: XBee.pin9, Attiny84.pin2
  N9: XBee.pin15, 220.Pin_0
  N10: Attiny84.pin3, 220_3.Pin_1
  N11: Attiny84.pin7, Sensor2.pin2
  N12: Attiny84.pin8, 220_6.Pin_0
  N13: Attiny84.pin9, Sensor2.pin4
  N14: Attiny84.pin10, J7.pin1
  N15: Attiny84.pin11, 220_5.Pin_0
  N16: Attiny84.pin12, 220_4.Pin_0
  N17: 220_4.Pin_1, LED4.anode
  N18: 220_5.Pin_1, LED5.anode
  N19: 220_6.Pin_1, LED6.anode
  N20: FET4.base, LED6.cathode
  N21: FET4.collector, D3.anode, J6.pin2
  N22: FET5.base, LED5.cathode
  N23: FET5.collector, D2.anode, J4.pin2
  N24: FET6.base, LED4.cathode
  N25: FET6.collector, D1.anode, J5.pin2
  N26: D2.cathode, D1.cathode, D3.cathode, J4.pin1, J5.pin1, J6.pin1, Power_plug1.VCC, U1.input_voltage

notes:
  exsertus.com
  XBeeDCPowerSwitch v1.0
  SCK
  GND
  SDA
  Vcc
  +
  IO4
