# Fritzing sketch XBeeEmonSensor84_1.0 (saved by Fritzing 0.8.3b)
circuit board: 5.91723cm x 3.06445cm
breadboards: 1

parts:
  Actv = LED - 3mm [color="Red (633nm)" package="3 mm [THT]"]
  RSSI = LED - 3mm [color="Red (633nm)" package="3 mm [THT]"]
  Assc = LED - 3mm [color="Red (633nm)" package="3 mm [THT]"]
  XBee = XBee
  3V3_Reg = female pin header, 3 pins [form="♀ (female)"]
  + = Battery
  +_2 = female pin header, 1 pin [form="♀ (female)"]
  - = female pin header, 1 pin [form="♀ (female)"]  # not connected
  Sensor = female pin header, 4 pins [form="♀ (female)"]
  Sensor1 = female pin header, 4 pins [form="♀ (female)"]
  Sensor2 = female pin header, 4 pins [form="♀ (female)"]
  Sensor3 = female pin header, 3 pins [form="♀ (female)"]
  Sensor4 = female pin header, 3 pins [form="♀ (female)"]
  Sensor5 = female pin header, 3 pins [form="♀ (female)"]
  Attiny84 = IC, DIP package, 14 pins [chip_label=Attiny84]
  220 = Resistor [tolerance=±5% resistance=220 package=THT]
  220_2 = Resistor [tolerance=±5% resistance=220 package=THT]
  220_3 = Resistor [tolerance=±5% resistance=220 package=THT]
  TRS1 = Audio Jack (TRS) 3.5mm [package="4Ucon 08780 [THT]"]  # not connected

nets:
  N1: Actv.anode, 220_3.Pin_0
  N2: RSSI.anode, 220_2.Pin_1
  N3: Assc.anode, 220.Pin_1
  N4: XBee.VCC, 3V3_Reg.pin2, Attiny84.pin1
  N5: XBee.pin2, Attiny84.pin5
  N6: XBee.pin3, Attiny84.pin6
  N7: XBee.pin6, 220_2.Pin_0
  N8: XBee.pin9, Attiny84.pin2
  N9: XBee.pin15, 220.Pin_0
  N10: 3V3_Reg.pin3, +.+, +_2.pin1
  N11: Sensor.pin1, Sensor1.pin1, Sensor2.pin1, Sensor3.pin2, Sensor4.pin2, Sensor5.pin2, Attiny84.pin3, 220_3.Pin_1
  N12: Sensor.pin2, Sensor1.pin2, Sensor2.pin2, Attiny84.pin7
  N13: Sensor.pin3, Sensor1.pin3, Sensor2.pin3
  N14: Sensor.pin4, Sensor1.pin4, Sensor2.pin4, Attiny84.pin9
  N15: Sensor3.pin1, Attiny84.pin11
  N16: Sensor4.pin1, Attiny84.pin8
  N17: Sensor5.pin1, Attiny84.pin12

notes:
  exsertus.com
  XBeeSensor84 v1.1
  -
  Vcc
  3v3
  Gnd
  Pin
  GND
  SCK
  SDA
  PWM
  ADC
