# Fritzing sketch XBeeSwitch+v1.0 (saved by Fritzing 0.9.0b)
circuit board: 5.34104cm x 3.38926cm
breadboards: 1

parts:
  XBee = XBee
  J1 = Screw terminal - 2 pins [package=THT]
  J2 = Screw terminal - 2 pins [package=THT]
  1K = Resistor [tolerance=±5% resistance=1k package=THT]
  1K_2 = Resistor [tolerance=±5% resistance=1k package=THT]
  Power = male pin header, 2 pins [form="♂ (male)"]
  3_3_Reg = Voltage Regulator - 3.3V [package="TO220 [THT]"]
  Q4 = pnp-Powertransistor [package="TO220 [THT]"]
  D1 = Rectifier Diode [part_number=1N4001 package="300 mil [THT]"]
  D2 = Rectifier Diode [part_number=1N4001 package="300 mil [THT]"]
  Q3 = pnp-Powertransistor [package="TO220 [THT]"]

nets:
  N1: XBee.VCC, 3_3_Reg.output_voltage
  N2: XBee.pin18, 1K_2.Pin_0
  N3: XBee.pin19, 1K.Pin_0
  N4: J1.pin1, J2.pin1, Power.pin2, 3_3_Reg.input_voltage, D1.cathode, D2.cathode
  N5: J1.pin2, D2.anode, Q3.collector
  N6: J2.pin2, Q4.collector, D1.anode
  N7: 1K.Pin_1, Q3.base
  N8: 1K_2.Pin_1, Q4.base

notes:
  +
  exsertus.com
  XBee Switch v1.0
  12v DC Max
