# Fritzing sketch XBeeTempHumMoistureSensor84_1.0 (saved by Fritzing 0.8.3b)
circuit board: 5.91723cm x 3.06445cm
breadboards: 1

parts:
  Actv = LED - 3mm [color="Red (633nm)" package="3 mm [THT]"]
  RSSI = LED - 3mm [color="Red (633nm)" package="3 mm [THT]"]
  Assc = LED - 3mm [color="Red (633nm)" package="3 mm [THT]"]
  XBee = XBee
  3V3_Reg = female pin header, 3 pins [form="♀ (female)"]
  + = female pin header, 1 pin [form="♀ (female)"]
  - = female pin header, 1 pin [form="♀ (female)"]  # not connected
  Sensor = female pin header, 4 pins [form="♀ (female)"]
  Sensor4 = female pin header, 3 pins [form="♀ (female)"]
  Attiny84 = IC, DIP package, 14 pins [chip_label=Attiny84]
  220 = Resistor [tolerance=±5% resistance=220 package=THT]
  220_2 = Resistor [tolerance=±5% resistance=220 package=THT]
  220_3 = Resistor [tolerance=±5% resistance=220 package=THT]
  J1 = Screw terminal - 2 pins [package=THT]
  RHT1 = Humidity and Temperature Sensor RHT03
  1K = Resistor [tolerance=±5% resistance=220 package=THT]
  10K = Resistor [tolerance=±5% resistance=220 package=THT]

nets:
  N1: Actv.anode, 220_3.Pin_0
  N2: RSSI.anode, 220_2.Pin_1
  N3: Assc.anode, 220.Pin_1
  N4: XBee.VCC, +.pin1, Attiny84.pin1
  N5: XBee.pin2, Attiny84.pin5
  N6: XBee.pin3, Attiny84.pin6
  N7: XBee.pin6, 220_2.Pin_0
  N8: XBee.pin9, Attiny84.pin2
  N9: XBee.pin15, 220.Pin_0
  N10: 3V3_Reg.pin2, Sensor.pin1, Sensor4.pin2, 220_3.Pin_1, J1.pin1, RHT1.Vcc, 1K.Pin_0
  N11: 3V3_Reg.pin3, Attiny84.pin3
  N12: Sensor.pin2, Attiny84.pin7
  N13: Sensor.pin4, Attiny84.pin9
  N14: Sensor4.pin1, Attiny84.pin8
  N15: Attiny84.pin11, J1.pin2, 10K.Pin_0
  N16: Attiny84.pin12, RHT1.Data-signal, 1K.Pin_1

notes:
  exsertus.com
  XBeeTHMSensor84 v1.0
  Vcc
  Gnd
  SCK
  GND
  SDA
  IO3
  3v3
