# Fritzing sketch XBeeTempMoist-85-1_0 (saved by Fritzing 0.9.0b)
circuit board: 2.60356cm x 4.54795cm
breadboards: 1

parts:
  10K = Resistor [tolerance=±5% resistance=220 package=THT]
  J1 = Screw terminal - 2 pins [package=THT]
  Actv = LED - 3mm [color="Red (633nm)" package="3 mm [THT]"]
  Assc = LED - 3mm [color="Red (633nm)" package="3 mm [THT]"]
  ATTiny85 = IC, DIP package, 8 pins [chip_label=IC]
  TMP36 = TMP36 Temperature Sensor [package="TO92 [THT]"]
  U1 = XBee
  220 = Resistor [tolerance=±5% resistance=220 package=THT]
  220_2 = Resistor [tolerance=±5% resistance=220 package=THT]
  - = female pin header, 1 pin [form="♀ (female)"]  # not connected
  + = female pin header, 1 pin [form="♀ (female)"]

nets:
  N1: 10K.Pin_0, J1.pin2, ATTiny85.pin3
  N2: J1.pin1, ATTiny85.pin5, TMP36.+Vs, 220.Pin_0
  N3: Actv.anode, 220.Pin_1
  N4: Assc.anode, 220_2.Pin_1
  N5: ATTiny85.pin2, U1.pin3
  N6: ATTiny85.pin6, U1.pin9
  N7: ATTiny85.pin7, TMP36.Vout
  N8: ATTiny85.pin8, U1.VCC, +.pin1
  N9: U1.pin15, 220_2.Pin_0

notes:
  exsertus.com
  XBeeTempMoistSensor v1.0
